# Fritzing sketch Balanceermeneer (saved by Fritzing 0.9.4)
breadboards: 1

parts:
  Arduino_Pro_Mini = Arduino Pro Mini v13
  DRV_1 = DRV 8825 Stepper Motor Carrier, High Current [part_number="DRV 8825"]
  DRV_2 = DRV 8825 Stepper Motor Carrier, High Current [part_number="DRV 8825"]
  NEMA_17 = Stepper Motor - Bipolar
  NEMA_17_2 = Stepper Motor - Bipolar
  M1 = RioRand LM2596
  12V_Spanningsbron = LIPO-2000mAh [package=lipo-2000]
  MPU6050 = InvenSense MPU6050
  C1 = Electrolytic Capacitor [capacitance=100μF package="0807 [SMD, electrolytic]"]
  C2 = Electrolytic Capacitor [capacitance=100μF package="0807 [SMD, electrolytic]"]

nets:
  VCC: Arduino_Pro_Mini.VCC, DRV_1.MS1, DRV_1.MS2, DRV_1.RESET, DRV_1.SLEEP, DRV_1.VOLTAGE_DD, DRV_2.MS1, DRV_2.MS2, DRV_2.RESET, DRV_2.SLEEP, DRV_2.VOLTAGE_DD, M1.Pin_3, MPU6050.VCC
  GND: Arduino_Pro_Mini.GND, DRV_1.GROUND_LOG, DRV_2.GROUND_LOG, M1.Pin_4, MPU6050.GND
  N1: Arduino_Pro_Mini.A4, MPU6050.SDA
  N2: Arduino_Pro_Mini.A5, MPU6050.SCL
  N3: Arduino_Pro_Mini.D5_PWM, DRV_2.DIRECTION
  N4: Arduino_Pro_Mini.D4, DRV_2.STEP
  N5: Arduino_Pro_Mini.D3_PWM, DRV_1.DIRECTION
  N6: Arduino_Pro_Mini.D2, DRV_1.STEP
  N7: DRV_1.VOLTAGE_ST/_MT, DRV_2.VOLTAGE_ST/_MT, M1.Pin_1, 12V_Spanningsbron.+, C1.-, C2.-
  N8: DRV_1.GROUND_ST/_MT, DRV_2.GROUND_ST/_MT, M1.Pin_2, 12V_Spanningsbron.-, C1.+, C2.+
  N9: DRV_1.OUT_2B, NEMA_17.A
  N10: DRV_1.OUT_2A, NEMA_17.C
  N11: DRV_1.OUT_1A, NEMA_17.B
  N12: DRV_1.OUT_1B, NEMA_17.D
  N13: DRV_2.OUT_2B, NEMA_17_2.A
  N14: DRV_2.OUT_2A, NEMA_17_2.C
  N15: DRV_2.OUT_1A, NEMA_17_2.B
  N16: DRV_2.OUT_1B, NEMA_17_2.D
